// Logisim project Programa_Principal.circ as structural Verilog
module ALU_1bit (
  input  Cin,
  input  [1:0] Code,
  input  A,
  input  B,
  output S,
  output Cout
);

  wire adder_1_cout, adder_1_out, and_1_out, or_1_out, subtractor_1_bout, subtractor_1_out;

  and and_1 (and_1_out, A, B);
  or or_1 (or_1_out, A, B);
  Adder #(.width(1)) adder_1 (.a(A), .b(B), .out(adder_1_out), .cin(Cin), .cout(adder_1_cout));
  Subtractor #(.width(1)) subtractor_1 (.a(A), .b(B), .out(subtractor_1_out), .bin(Cin), .bout(subtractor_1_bout));
  Multiplexer #(.select(2)) multiplexer_1 (
    .in0(and_1_out), .in1(or_1_out), .in2(adder_1_out), .in3(subtractor_1_out), .out(S), .sel(Code));
  Multiplexer #(.select(2)) multiplexer_2 (
    .in0(1'b0), .in1(1'b0), .in2(adder_1_cout), .in3(subtractor_1_bout), .out(Cout), .sel(Code));
endmodule

module ALU_8bits (
  input  [7:0] A,
  input  [7:0] B,
  input  [1:0] in_3,
  input  in_4,
  output [7:0] S,
  output Cout
);

  wire alu_1bit_1_cout, alu_1bit_2_cout, alu_1bit_3_cout, alu_1bit_4_cout, alu_1bit_5_cout, alu_1bit_6_cout,
       alu_1bit_7_cout;

  ALU_1bit alu_1bit_1 (.Cin(in_4), .Code(in_3), .A(A[0]), .B(B[0]), .S(S[0]), .Cout(alu_1bit_1_cout));
  ALU_1bit alu_1bit_2 (.Cin(alu_1bit_1_cout), .Code(in_3), .A(A[1]), .B(B[1]), .S(S[1]), .Cout(alu_1bit_2_cout));
  ALU_1bit alu_1bit_3 (.Cin(alu_1bit_2_cout), .Code(in_3), .A(A[2]), .B(B[2]), .S(S[2]), .Cout(alu_1bit_3_cout));
  ALU_1bit alu_1bit_4 (.Cin(alu_1bit_3_cout), .Code(in_3), .A(A[3]), .B(B[3]), .S(S[3]), .Cout(alu_1bit_4_cout));
  ALU_1bit alu_1bit_5 (.Cin(alu_1bit_4_cout), .Code(in_3), .A(A[4]), .B(B[4]), .S(S[4]), .Cout(alu_1bit_5_cout));
  ALU_1bit alu_1bit_6 (.Cin(alu_1bit_5_cout), .Code(in_3), .A(A[5]), .B(B[5]), .S(S[5]), .Cout(alu_1bit_6_cout));
  ALU_1bit alu_1bit_7 (.Cin(alu_1bit_6_cout), .Code(in_3), .A(A[6]), .B(B[6]), .S(S[6]), .Cout(alu_1bit_7_cout));
  ALU_1bit alu_1bit_8 (.Cin(alu_1bit_7_cout), .Code(in_3), .A(A[7]), .B(B[7]), .S(S[7]), .Cout(Cout));
endmodule

module Registro_8bits (
  input  [7:0] in_1,
  input  in_2,
  input  [7:0] D_in,
  input  CLK,
  input  CLEAR,
  output [7:0] out_6,
  output [7:0] Q_out
);

  Register register_1 (.D(in_1), .en(1'b1), .clk(in_2), .Q(out_6));  // open: clr
  D_Flip_Flop d_ff_1 (.D(D_in[7]), .clk(CLK), .Q(Q_out[7]), .reset(CLEAR));  // open: Qn, preset
  D_Flip_Flop d_ff_2 (.D(D_in[6]), .clk(CLK), .Q(Q_out[6]), .reset(CLEAR));  // open: Qn, preset
  D_Flip_Flop d_ff_3 (.D(D_in[5]), .clk(CLK), .Q(Q_out[5]), .reset(CLEAR));  // open: Qn, preset
  D_Flip_Flop d_ff_4 (.D(D_in[4]), .clk(CLK), .Q(Q_out[4]), .reset(CLEAR));  // open: Qn, preset
  D_Flip_Flop d_ff_5 (.D(D_in[3]), .clk(CLK), .Q(Q_out[3]), .reset(CLEAR));  // open: Qn, preset
  D_Flip_Flop d_ff_6 (.D(D_in[2]), .clk(CLK), .Q(Q_out[2]), .reset(CLEAR));  // open: Qn, preset
  D_Flip_Flop d_ff_7 (.D(D_in[1]), .clk(CLK), .Q(Q_out[1]), .reset(CLEAR));  // open: Qn, preset
  D_Flip_Flop d_ff_8 (.D(D_in[0]), .clk(CLK), .Q(Q_out[0]), .reset(CLEAR));  // open: Qn, preset
endmodule
